// Logisim project cod practical 7 and 8.circ as structural Verilog: 1 circuit, main circuit main
module main (
  output out_1,
  output out_2,
  output out_3,
  output out_4,
  output out_5,
  output out_6,
  output out_7,
  output out_8
);

  wire and_1_out, and_2_out, clock_1_out, clock_2_out;

  Clock clock_1 (.out(clock_1_out));
  Clock clock_2 (.out(clock_2_out));
  J_K_Flip_Flop j_k_ff_1 (.J(1'b1), .clk(clock_1_out), .K(1'b1), .Q(out_1));  // open: Qn, preset, en, reset
  D_Flip_Flop d_ff_1 (.clk(clock_2_out), .D(1'b1), .Q(out_6));  // open: Qn, preset, en, reset
  J_K_Flip_Flop j_k_ff_2 (.J(out_1), .clk(clock_1_out), .K(clock_1_out), .Qn(out_2));  // open: Q, preset, en, reset
  D_Flip_Flop d_ff_2 (.clk(clock_2_out), .D(out_6), .Q(out_7));  // open: Qn, preset, en, reset
  buf and_1 (and_1_out, out_2);  // AND_Gate
  D_Flip_Flop d_ff_3 (.clk(clock_2_out), .D(out_7), .Q(out_8));  // open: Qn, preset, en, reset
  J_K_Flip_Flop j_k_ff_3 (.clk(clock_1_out), .K(and_1_out), .Q(out_3));  // open: J, Qn, preset, en, reset
  D_Flip_Flop d_ff_4 (.clk(clock_2_out), .D(out_8), .Qn(out_5));  // open: Q, preset, en, reset
  and and_2 (and_2_out, and_1_out, out_3);
  J_K_Flip_Flop j_k_ff_4 (.clk(clock_1_out), .K(and_2_out), .Qn(out_4));  // open: J, Q, preset, en, reset

  // Notes on the sheet:
  //   4 bit counters with J-K flip flop
  //   4 bit counters with d flip flop
endmodule
